# Fritzing sketch jp-node-board (saved by Fritzing 0.9.2b)
circuit board: 4.68371cm x 3.12866cm
breadboards: 1

parts:
  Homie_TempLux = WeMos D1 Mini
  D2 = LED - 5mm [color="Red (633nm)" package="5 mm [THT]"]
  R1 = Resistor [tolerance=±5% resistance=220 package=THT]
  Lux = female pin header, 3 pins [form="♀ (female)"]
  T1 = female pin header, 3 pins [form="♀ (female)"]
  R2 = Resistor [tolerance=±5% resistance=220 package=THT]

nets:
  N1: Homie_TempLux.3V3, Lux.pin3, T1.pin2, R2.Pin_0
  N2: Homie_TempLux.D2, R1.Pin_1
  N3: Homie_TempLux.D3, T1.pin3, R2.Pin_1
  N4: Homie_TempLux.D6, Lux.pin1
  N5: Homie_TempLux.G, D2.cathode, Lux.pin2, T1.pin1
  N6: D2.anode, R1.Pin_0

notes:
  Homie/LT
  D2
  +
  D
  G + D
  68
  4.7k
  lux
  DS18B20
